# Fritzing sketch CircuitDesign-fritzingSourceFile (saved by Fritzing 0.9.4)
breadboards: 1

parts:
  Raspberry_Pi_1 = Raspberry Pi Zero  # not connected
  Raspberry_Pi_2 = Raspberry Pi Zero  # not connected
  Raspberry_Pi_3 = Raspberry Pi 3 [part_number=RPI-3-V1.2]
  LED1 = LED - 5mm [color="Yellow (595nm)" package="5 mm [THT]"]
  LED2 = LED - 5mm [color="Yellow (595nm)" package="5 mm [THT]"]
  LED3 = LED - 5mm [color="Yellow (595nm)" package="5 mm [THT]"]
  LED4 = LED - 5mm [color="Yellow (595nm)" package="5 mm [THT]"]

nets:
  N1: Raspberry_Pi_3.GPIO4, LED4.anode
  N2: Raspberry_Pi_3.GPIO17, LED3.anode
  N3: Raspberry_Pi_3.GPIO27, LED2.anode
  N4: Raspberry_Pi_3.GPIO5, LED1.anode
  N5: Raspberry_Pi_3.GND, LED1.cathode, LED2.cathode, LED3.cathode, LED4.cathode
